// Logisim project Circuit1.circ as structural Verilog: 1 circuit, main circuit main
module main (
  input  A,
  input  B,
  input  C,
  input  D,
  input  in_5,
  input  in_6,
  input  in_7,
  input  in_8,
  input  in_9
);

  wire and_1_out, and_2_out, and_3_out, and_4_out, and_5_out, and_6_out, and_7_out, not_1_out, not_2_out,
       not_3_out, not_4_out, not_5_out, not_6_out, not_7_out, or_1_out, or_2_out, xor_1_out;

  not not_1 (not_1_out, B);
  and and_1 (and_1_out, not_1_out, C);
  or or_1 (or_1_out, A, and_1_out, and_2_out, and_3_out);
  not not_2 (not_2_out, C);
  and and_2 (and_2_out, B, not_2_out);
  not not_3 (not_3_out, C);
  not not_4 (not_4_out, D);
  and and_3 (and_3_out, C, not_4_out);
  not not_5 (not_5_out, B);
  and and_4 (and_4_out, not_5_out, not_7_out);
  and and_5 (and_5_out, not_3_out, D);
  not not_6 (not_6_out, A);
  not not_7 (not_7_out, and_5_out);
  and and_6 (and_6_out, not_6_out, B);
  or or_2 (or_2_out, and_4_out, and_7_out);
  _7_Segment_Display u_7_segment_display_1 (
    .g(or_1_out), .f(in_8), .a(in_7), .b(in_5), .e(in_6), .d(or_2_out), .c(in_9));  // open: dp
  xor xor_1 (xor_1_out, C, D);
  and and_7 (and_7_out, and_6_out, xor_1_out);

  // Notes on the sheet:
  //   Middle
  //   B'&(C'D)'
  //   Bottom
endmodule
