// Logisim project Circuit2.circ as structural Verilog: 1 circuit, main circuit main
module main (
  input  A,
  input  B,
  input  C,
  input  D
);

  wire and_1_out, and_2_out, and_3_out, and_4_out, and_5_out, and_6_out, and_7_out, and_8_out, B_prime_C_out,
       B_prime_D_prime_out, BC_prime_D_out, BD_prime_out, C_prime_D_prime_out, CD_out, not_1_out, not_2_out,
       not_3_out, not_4_out, not_5_out, not_6_out, not_7_out, not_8_out, not_9_out, not_10_out, not_11_out,
       not_12_out, not_13_out, not_14_out, not_15_out, or_1_out, or_2_out, or_3_out, or_4_out, or_5_out,
       or_6_out, or_7_out;

  not not_1 (not_1_out, B);
  not not_2 (not_2_out, B);
  not not_3 (not_3_out, B);
  and BD_prime (BD_prime_out, B, not_4_out);
  not not_4 (not_4_out, D);
  and B_prime_C (B_prime_C_out, not_1_out, C);
  and and_1 (and_1_out, C_prime_D_prime_out, not_2_out);
  not not_5 (not_5_out, B);
  not not_6 (not_6_out, D);
  and and_2 (and_2_out, not_3_out, CD_out);
  not not_7 (not_7_out, C);
  and and_3 (and_3_out, B, not_7_out);
  and B_prime_D_prime (B_prime_D_prime_out, not_5_out, not_6_out);
  and BC_prime_D (BC_prime_D_out, D, D, and_3_out);
  not not_8 (not_8_out, D);
  and and_4 (and_4_out, C, not_8_out);
  _7_Segment_Display u_7_segment_display_1 (
    .g(or_2_out), .f(or_1_out), .a(or_5_out), .b(or_6_out), .e(or_3_out), .d(or_4_out), .c(or_7_out));  // open: dp
  or or_1 (or_1_out, A, C_prime_D_prime_out, and_3_out, BD_prime_out);
  or or_2 (or_2_out, A, and_4_out, and_3_out, B_prime_C_out);
  or or_3 (or_3_out, and_4_out, and_1_out);
  or or_4 (or_4_out, B_prime_D_prime_out, BC_prime_D_out, and_2_out, and_4_out);
  and CD (CD_out, C, D);
  not not_9 (not_9_out, C);
  or or_5 (or_5_out, A, C, and_5_out, and_6_out);
  and and_5 (and_5_out, C_prime_D_prime_out, not_11_out);
  or or_6 (or_6_out, A, and_7_out, CD_out, C_prime_D_prime_out);
  or or_7 (or_7_out, and_8_out, CD_out, not_14_out);
  not not_10 (not_10_out, D);
  and C_prime_D_prime (C_prime_D_prime_out, not_9_out, not_10_out);
  not not_11 (not_11_out, B);
  and and_6 (and_6_out, and_3_out, D);
  not not_12 (not_12_out, A);
  and and_7 (and_7_out, not_12_out, not_13_out);
  not not_13 (not_13_out, B);
  and and_8 (and_8_out, not_15_out, B);
  not not_14 (not_14_out, C);
  not not_15 (not_15_out, A);

  // Notes on the sheet:
  //   A,B,C,D,BC',CD',CD,C'D'
  //   B'C'D'
  //   B'CD
  //   Top Left
  //   Middle
  //   Bottom Left
  //   Bottom
  //   BC'
  //   CD'
  //   Top
  //   Top Right
  //   Bottom Right
  //   B'C'D'
  //   A'B
  //   BCD'
endmodule
